# Fritzing sketch Factorio_turret (saved by Fritzing 0.9.9b)
breadboards: 1

parts:
  Part1 = Arduino Nano (Rev3.0) (ICSP)
  L293D_Motor_Driver = L293D [package=THT]
  Power_plug1 = Power plug
  Q1 = TRANSISTOR_NPN [package=to-92-ammo]
  Lift_system_Motor = DC Motor with two-phase hall-encoder [part_number=VT-E-G25A-06-177E]
  Gun_Barrel_Motor = DC Motor
  R1 = Resistor [tolerance=±5% power=0.25 resistance=1k package=THT]
  Turret_rotation_motor = DC Motor
  D2F1 = D2F-FL Omron Snap Action Limit Switch with Level
  R2 = Resistor [tolerance=±5% power=0.25 resistance=1k package=THT]

nets:
  GND: Part1.GND, L293D_Motor_Driver.0V, Power_plug1.GND, Q1.E, Lift_system_Motor.pin5, R2.Pin_1
  N1: Part1.D2, Lift_system_Motor.pin3
  N2: Part1.D3, Lift_system_Motor.pin4
  N3: Part1.D4, L293D_Motor_Driver.In_2
  N4: Part1.D5, L293D_Motor_Driver.In_1
  N5: Part1.D6, L293D_Motor_Driver.In_3
  N6: Part1.D7, L293D_Motor_Driver.In_4
  N7: Part1.D8, D2F1.NO, R2.Pin_0
  N8: Part1.D10, R1.Pin_1
  N9: Part1.5V, L293D_Motor_Driver.Enable_1, L293D_Motor_Driver.Enable_2, L293D_Motor_Driver.+V, D2F1.COM
  N10: Part1.3V3, Lift_system_Motor.pin2
  N11: L293D_Motor_Driver.Out_1_(_Controlled_by_Enable_1_), Turret_rotation_motor.pin_2
  N12: L293D_Motor_Driver.Out_2_(_Controlled_by_Enable_1_), Turret_rotation_motor.pin_1
  N13: L293D_Motor_Driver.+Vmotor, Power_plug1.VCC, Gun_Barrel_Motor.pin_1
  N14: L293D_Motor_Driver.Out_3_(_Controlled_by_Enable_2_), Lift_system_Motor.pin1
  N15: L293D_Motor_Driver.Out_4_(_Controlled_by_Enable_2_), Lift_system_Motor.pin6
  N16: Q1.B, R1.Pin_0
  N17: Q1.C, Gun_Barrel_Motor.pin_2

custom parts:
  D2F-FL Omron Snap Action Limit Switch with Level: Snap action switch with stainless steel lever.
